# Fritzing sketch motherboard_5v (saved by Fritzing 0.9.3b)
circuit board: 9cm x 6cm
breadboards: 1

parts:
  VCC1 = Battery
  IC1 = L293D [package=THT]
  J2 = female pin header, 3 pins [form="♀ (female)"]
  J3 = female pin header, 3 pins [form="♀ (female)"]
  J4 = female pin header, 3 pins [form="♀ (female)"]
  M1 = Screw terminal - 2 pins [package=THT]
  M2 = Screw terminal - 2 pins [package=THT]
  IC2 = IC, DIP package, 14 pins [chip_label=attinyX4]
  C1 = Electrolytic Capacitor [capacitance=0.1mF package="100 mil [THT, electrolytic]"]
  J1 = shrouded pin header, 10 pins [form="♂ (shrouded male)"]
  C2 = Ceramic Capacitor [capacitance=100nF package="100 mil [THT, multilayer]"]
  R1 = Resistor [tolerance=±5% resistance=10k package=THT]
  C3 = Electrolytic Capacitor [capacitance=1µF package="100 mil [THT, electrolytic]"]
  J5 = female pin header, 3 pins [form="♀ (female)"]
  J6 = female pin header, 3 pins [form="♀ (female)"]
  RESET = Pushbutton [package="[THT]"]
  R2 = Resistor [tolerance=±5% resistance=220 package=THT]
  LED1 = LED - 5mm [color="Red (633nm)" package="5 mm [THT]"]
  U1 = Voltage Regulator - 5V [package="TO220 [THT]"]
  ON/OFF = Toggle Switch [package=THT]

nets:
  GND: VCC1.-, IC1.0V, J2.pin1, J3.pin1, J4.pin1, IC2.pin14, C1.-, J1.pin6, C2.1, C3.-, J5.pin1, J6.pin1, RESET.Pin_3, RESET.Pin_4, LED1.cathode, U1.GND
  N1: VCC1.+, ON/OFF.L1, ON/OFF.COM
  N2: IC1.Enable_1, IC2.pin8, J1.pin5
  N3: IC1.In_1, IC2.pin10
  N4: IC1.Out_1_(_Controlled_by_Enable_1_), M1.pin2
  N5: IC1.Out_2_(_Controlled_by_Enable_1_), M1.pin1
  N6: IC1.In_2, IC2.pin9, J1.pin4
  N7: IC1.+Vmotor, C1.+, R2.Pin_1, U1.input_voltage, ON/OFF.L2
  N8: IC1.Enable_2, IC2.pin7, J1.pin1
  N9: IC1.In_3, IC2.pin6
  N10: IC1.Out_3_(_Controlled_by_Enable_2_), M2.pin2
  N11: IC1.Out_4_(_Controlled_by_Enable_2_), M2.pin1
  N12: IC1.In_4, IC2.pin5
  N13: IC1.+V, J2.pin2, J3.pin2, J4.pin2, IC2.pin1, R1.Pin_1, C3.+, J5.pin2, J6.pin2, U1.output_voltage
  N14: J2.pin3, IC2.pin11
  N15: J3.pin3, IC2.pin12
  N16: J4.pin3, IC2.pin13
  N17: IC2.pin2, J5.pin3
  N18: IC2.pin3, J6.pin3
  N19: IC2.pin4, J1.pin3, C2.0, R1.Pin_0, RESET.Pin_1, RESET.Pin_2
  N20: R2.Pin_0, LED1.anode
