# Fritzing sketch sensor (saved by Fritzing 0.9.2b)
circuit board: 2cm x 3cm
breadboards: 1

parts:
  Q1 = LTR-301 [package=ltr-301]
  LED1 = LED - 3mm [color="Red (633nm)" package="3 mm [THT]"]
  J1 = female pin header, 3 pins [form="♀ (female)"]
  R1 = Resistor [tolerance=±5% resistance=220 package=THT]
  R2 = Resistor [tolerance=±5% resistance=100k package=THT]

nets:
  N1: Q1.C, LED1.cathode, J1.pin1
  N2: Q1.E, J1.pin3, R2.Pin_1
  N3: LED1.anode, R1.Pin_1
  N4: J1.pin2, R1.Pin_0, R2.Pin_0
